// Logisim project лаб 2.circ as structural Verilog: 5 circuits, main circuit main
module main (
  input  _0,
  input  _1,
  input  _2,
  input  _3,
  input  _4,
  input  _5,
  input  _6,
  input  _7,
  input  _8,
  input  _9,
  input  _0_2,
  input  _1_2,
  input  _2_2,
  input  _3_2,
  input  _4_2,
  input  _5_2,
  input  _6_2,
  input  _7_2,
  input  _8_2,
  input  _9_2,
  input  in_21
);

  wire and_1_out, and_2_out, and_3_out, \n4_бітний_суматор_1_out_10 , \n4_бітний_суматор_1_out_11 ,
       \n4_бітний_суматор_1_out_12 , \n4_бітний_суматор_1_out_13 , \n4_бітний_суматор_1_out_14 , not_1_out,
       xor_1_out, xor_2_out, xor_3_out, xor_4_out, \шифратор_1_q1 , \шифратор_1_q2 , \шифратор_1_q4 ,
       \шифратор_1_q8 , \шифратор_2_q1 , \шифратор_2_q2 , \шифратор_2_q4 , \шифратор_2_q8 ;
  wire [3:0] controlled_buffer_1_out, controlled_inverter_1_out;

  \Шифратор  \u_шифратор_1  (
    ._0(_0), ._1(_1), ._2(_2), ._3(_3), ._4(_4), ._5(_5), ._6(_6), ._7(_7), ._8(_8), ._9(_9),
    .Q8(\шифратор_1_q8 ), .Q4(\шифратор_1_q4 ), .Q2(\шифратор_1_q2 ), .Q1(\шифратор_1_q1 ));
  \Шифратор  \u_шифратор_2  (
    ._0(_0_2), ._1(_1_2), ._2(_2_2), ._3(_3_2), ._4(_4_2), ._5(_5_2), ._6(_6_2), ._7(_7_2), ._8(_8_2),
    ._9(_9_2), .Q8(\шифратор_2_q8 ), .Q4(\шифратор_2_q4 ), .Q2(\шифратор_2_q2 ), .Q1(\шифратор_2_q1 ));
  xor xor_1 (xor_1_out, \шифратор_2_q8 , in_21);
  xor xor_2 (xor_2_out, \шифратор_2_q4 , in_21);
  xor xor_3 (xor_3_out, \шифратор_2_q2 , in_21);
  xor xor_4 (xor_4_out, \шифратор_2_q1 , in_21);
  and and_1 (and_1_out, \n4_бітний_суматор_1_out_14 , and_3_out, and_3_out, in_21, in_21);
  \_4_бітний_суматор  \u_4_бітний_суматор_1  (
    .in_1(\шифратор_1_q8 ), .in_2(\шифратор_1_q4 ), .in_3(\шифратор_1_q2 ), .in_4(\шифратор_1_q1 ),
    .in_5(xor_1_out), .in_6(xor_2_out), .in_7(xor_3_out), .in_8(xor_4_out), .in_9(and_1_out),
    .out_10(\n4_бітний_суматор_1_out_10 ), .out_11(\n4_бітний_суматор_1_out_11 ),
    .out_12(\n4_бітний_суматор_1_out_12 ), .out_13(\n4_бітний_суматор_1_out_13 ),
    .out_14(\n4_бітний_суматор_1_out_14 ));
  // Probe on \n4_бітний_суматор_1_out_14 
  // Probe on and_1_out
  assign controlled_buffer_1_out[0] = not_1_out ? \n4_бітний_суматор_1_out_13  : 1'bz;  // Controlled_Buffer controlled_buffer_1
  assign controlled_buffer_1_out[1] = not_1_out ? \n4_бітний_суматор_1_out_12  : 1'bz;  // Controlled_Buffer controlled_buffer_2
  assign controlled_buffer_1_out[2] = not_1_out ? \n4_бітний_суматор_1_out_11  : 1'bz;  // Controlled_Buffer controlled_buffer_3
  assign controlled_buffer_1_out[3] = not_1_out ? \n4_бітний_суматор_1_out_10  : 1'bz;  // Controlled_Buffer controlled_buffer_4
  not not_1 (not_1_out, and_2_out);
  Hex_Digit_Display hex_digit_display_1 (.value(controlled_buffer_1_out));  // open: dp
  and and_2 (and_2_out, ~\n4_бітний_суматор_1_out_14 , in_21, in_21, in_21, in_21);  // AND_Gate
  and and_3 (and_3_out, \n4_бітний_суматор_1_out_14 , \n4_бітний_суматор_1_out_14 , in_21, in_21, in_21);
  assign controlled_inverter_1_out[0] = and_2_out ? ~\n4_бітний_суматор_1_out_13  : 1'bz;  // Controlled_Inverter controlled_inverter_1
  assign controlled_inverter_1_out[1] = and_2_out ? ~\n4_бітний_суматор_1_out_12  : 1'bz;  // Controlled_Inverter controlled_inverter_2
  assign controlled_inverter_1_out[2] = and_2_out ? ~\n4_бітний_суматор_1_out_11  : 1'bz;  // Controlled_Inverter controlled_inverter_3
  assign controlled_inverter_1_out[3] = and_2_out ? ~\n4_бітний_суматор_1_out_10  : 1'bz;  // Controlled_Inverter controlled_inverter_4
  Hex_Digit_Display hex_digit_display_2 ();  // open: value, dp
  Hex_Digit_Display hex_digit_display_3 (.value(controlled_inverter_1_out));  // open: dp
endmodule

module \Шифратор  (
  input  _0,
  input  _1,
  input  _2,
  input  _3,
  input  _4,
  input  _5,
  input  _6,
  input  _7,
  input  _8,
  input  _9,
  output Q8,
  output Q4,
  output Q2,
  output Q1
);

  or or_1 (Q8, _9, _8);
  or or_2 (Q4, _7, _6, _5, _4);
  or or_3 (Q2, _7, _6, _3, _2);
  or or_4 (Q1, _9, _7, _5, _3, _1);
endmodule

module \Дешифратор  (
  input  D1,
  input  D2,
  input  D3,
  input  D4,
  output _0,
  output _1,
  output _2,
  output _3,
  output _4,
  output _5,
  output _6,
  output _7,
  output _8,
  output _9
);

  wire not_1_out, not_2_out, not_3_out, not_4_out;

  not not_1 (not_1_out, D1);
  not not_2 (not_2_out, D2);
  not not_3 (not_3_out, D3);
  not not_4 (not_4_out, D4);
  // Probe on D1
  // Probe on not_1_out
  // Probe on D2
  // Probe on not_2_out
  // Probe on D3
  // Probe on not_3_out
  // Probe on D4
  // Probe on not_4_out
  and and_1 (_0, not_1_out, not_2_out, not_3_out, not_4_out, not_4_out);
  and and_2 (_1, D1, not_2_out, not_2_out, not_3_out, not_4_out);
  and and_3 (_2, not_1_out, D2, not_3_out, not_4_out, not_4_out);
  and and_4 (_3, D1, D2, not_3_out, not_4_out, not_4_out);
  and and_5 (_4, not_1_out, not_2_out, D3, not_4_out, not_4_out);
  and and_6 (_5, D1, D1, not_2_out, D3, not_4_out);
  and and_7 (_6, not_1_out, D2, D3, not_4_out, not_4_out);
  and and_8 (_7, D1, D2, D3, not_4_out, not_4_out);
  and and_9 (_8, D4, not_3_out, not_2_out, not_1_out, not_1_out);
  and and_10 (_9, D1, not_2_out, not_3_out, D4, D4);

  // Notes on the sheet:
  //   D1~D1
  //   D4~D4
  //   D2~D2
  //   D8~D8
endmodule

module \Повний_суматор  (
  input  Pi,
  input  a,
  input  b,
  output S,
  output P
);

  wire and_1_out, and_2_out, xor_1_out;

  xor xor_1 (xor_1_out, a, b);
  and and_1 (and_1_out, a, b);
  and and_2 (and_2_out, Pi, xor_1_out);
  xor xor_2 (S, Pi, xor_1_out);
  xor xor_3 (P, and_2_out, and_1_out);
endmodule

module \_4_бітний_суматор  (
  input  in_1,
  input  in_2,
  input  in_3,
  input  in_4,
  input  in_5,
  input  in_6,
  input  in_7,
  input  in_8,
  input  in_9,
  output out_10,
  output out_11,
  output out_12,
  output out_13,
  output out_14
);

  wire \повний_суматор_2_p , \повний_суматор_3_p , \повний_суматор_4_p ;

  \Повний_суматор  \u_повний_суматор_1  (.Pi(\повний_суматор_2_p ), .a(in_1), .b(in_5), .S(out_10), .P(out_14));
  \Повний_суматор  \u_повний_суматор_2  (
    .Pi(\повний_суматор_3_p ), .a(in_2), .b(in_6), .S(out_11), .P(\повний_суматор_2_p ));
  \Повний_суматор  \u_повний_суматор_3  (
    .Pi(\повний_суматор_4_p ), .a(in_3), .b(in_7), .S(out_12), .P(\повний_суматор_3_p ));
  \Повний_суматор  \u_повний_суматор_4  (.Pi(in_9), .a(in_4), .b(in_8), .S(out_13), .P(\повний_суматор_4_p ));
endmodule
