// Logisim project лаб 4.circ as structural Verilog
module \_1_бітний_компоратор  (
  input  a,
  input  b,
  output a_b,
  output a_b_2
);

  xnor xnor_1 (a_b, a, b);
  and and_1 (a_b_2, a, ~b);  // AND_Gate
endmodule

module \_4_бітний_суматор  (
  input  a0,
  input  in_2,
  input  in_3,
  input  a8,
  input  b0,
  input  in_6,
  input  in_7,
  input  b8,
  output a_b,
  output a_b_2,
  output a_b_3
);

  wire and_2_out, and_3_out, and_4_out, \n1_бітний_компоратор_1_a_b , \n1_бітний_компоратор_1_a_b_2 ,
       \n1_бітний_компоратор_2_a_b , \n1_бітний_компоратор_2_a_b_2 , \n1_бітний_компоратор_3_a_b ,
       \n1_бітний_компоратор_3_a_b_2 , \n1_бітний_компоратор_4_a_b , \n1_бітний_компоратор_4_a_b_2 ;

  \_1_бітний_компоратор  \u_1_бітний_компоратор_1  (
    .a(a0), .b(b0), .a_b(\n1_бітний_компоратор_1_a_b ), .a_b_2(\n1_бітний_компоратор_1_a_b_2 ));
  \_1_бітний_компоратор  \u_1_бітний_компоратор_2  (
    .a(in_2), .b(in_6), .a_b(\n1_бітний_компоратор_2_a_b ), .a_b_2(\n1_бітний_компоратор_2_a_b_2 ));
  \_1_бітний_компоратор  \u_1_бітний_компоратор_3  (
    .a(in_3), .b(in_7), .a_b(\n1_бітний_компоратор_3_a_b ), .a_b_2(\n1_бітний_компоратор_3_a_b_2 ));
  \_1_бітний_компоратор  \u_1_бітний_компоратор_4  (
    .a(a8), .b(b8), .a_b(\n1_бітний_компоратор_4_a_b ), .a_b_2(\n1_бітний_компоратор_4_a_b_2 ));
  and and_1 (a_b, \n1_бітний_компоратор_1_a_b , \n1_бітний_компоратор_2_a_b , \n1_бітний_компоратор_3_a_b , \n1_бітний_компоратор_4_a_b );
  and and_2 (and_2_out, \n1_бітний_компоратор_1_a_b_2 , \n1_бітний_компоратор_2_a_b , \n1_бітний_компоратор_3_a_b , \n1_бітний_компоратор_4_a_b );
  and and_3 (and_3_out, \n1_бітний_компоратор_2_a_b_2 , \n1_бітний_компоратор_3_a_b , \n1_бітний_компоратор_4_a_b );
  and and_4 (and_4_out, \n1_бітний_компоратор_3_a_b_2 , \n1_бітний_компоратор_4_a_b );
  or or_1 (a_b_3, and_2_out, and_3_out, and_4_out, \n1_бітний_компоратор_4_a_b_2 );
  nor nor_1 (a_b_2, a_b, a_b_3);
endmodule

module \_4_бітний_компоратор_та_шифратор  (
  input  in_1,
  input  in_2,
  input  in_3,
  input  in_4,
  input  in_5,
  input  in_6,
  input  in_7,
  input  in_8,
  input  in_9,
  input  in_10,
  input  in_11,
  input  in_12,
  input  in_13,
  input  in_14,
  input  in_15,
  input  in_16,
  input  in_17,
  input  in_18,
  input  in_19,
  input  in_20
);

  wire \n4_бітний_суматор_1_a_b , \n4_бітний_суматор_1_a_b_2 , \n4_бітний_суматор_1_a_b_3 , \шифратор_1_q1 ,
       \шифратор_1_q2 , \шифратор_1_q4 , \шифратор_1_q8 , \шифратор_2_q1 , \шифратор_2_q2 , \шифратор_2_q4 ,
       \шифратор_2_q8 ;

  \Шифратор  \u_шифратор_1  (
    ._0(in_1), ._1(in_2), ._2(in_3), ._3(in_4), ._4(in_5), ._5(in_5), ._6(in_7), ._7(in_8), ._8(in_9),
    ._9(in_10), .Q8(\шифратор_1_q8 ), .Q4(\шифратор_1_q4 ), .Q2(\шифратор_1_q2 ), .Q1(\шифратор_1_q1 ));
  \Шифратор  \u_шифратор_2  (
    ._0(in_11), ._1(in_12), ._2(in_13), ._3(in_14), ._4(in_15), ._5(in_16), ._6(in_17), ._7(in_18),
    ._8(in_19), ._9(in_20), .Q8(\шифратор_2_q8 ), .Q4(\шифратор_2_q4 ), .Q2(\шифратор_2_q2 ),
    .Q1(\шифратор_2_q1 ));
  LED led_1 (.in(\n4_бітний_суматор_1_a_b ));
  \_4_бітний_суматор  \u_4_бітний_суматор_1  (
    .a0(\шифратор_1_q1 ), .in_2(\шифратор_1_q2 ), .in_3(\шифратор_1_q4 ), .a8(\шифратор_1_q8 ),
    .b0(\шифратор_2_q1 ), .in_6(\шифратор_2_q2 ), .in_7(\шифратор_2_q4 ), .b8(\шифратор_2_q8 ),
    .a_b(\n4_бітний_суматор_1_a_b ), .a_b_2(\n4_бітний_суматор_1_a_b_2 ), .a_b_3(\n4_бітний_суматор_1_a_b_3 ));
  LED led_2 (.in(\n4_бітний_суматор_1_a_b_2 ));
  LED led_3 (.in(\n4_бітний_суматор_1_a_b_3 ));

  assign in_6 = in_5;
endmodule

module \множення  (
  input  a8,
  input  a4,
  input  a2,
  input  a1,
  input  b2,
  input  b4,
  input  b8,
  input  b1,
  output _128,
  output _64,
  output _32,
  output _16,
  output _8,
  output _4,
  output _2,
  output _1
);

  wire and_1_out, and_2_out, and_3_out, and_5_out, and_6_out, and_7_out, and_8_out, and_9_out, and_10_out,
       and_11_out, and_12_out, and_13_out, and_14_out, and_15_out, and_16_out, \n4_бітний_суматор_1_out_10 ,
       \n4_бітний_суматор_1_out_11 , \n4_бітний_суматор_1_out_12 , \n4_бітний_суматор_1_out_14 ,
       \n4_бітний_суматор_2_out_10 , \n4_бітний_суматор_2_out_11 , \n4_бітний_суматор_2_out_12 ,
       \n4_бітний_суматор_2_out_14 ;

  and and_1 (and_1_out, a8, b1);
  buf and_2 (and_2_out, b1);  // AND_Gate
  buf and_3 (and_3_out, b1);  // AND_Gate
  and and_4 (_1, a1, b1);
  and and_5 (and_5_out, a8, b2);
  and and_6 (and_6_out, a4, b2);
  and and_7 (and_7_out, a2, b2);
  and and_8 (and_8_out, a1, b2);
  \лаб_2_4_бітний_суматор  \u_4_бітний_суматор_1  (
    .in_1(and_5_out), .in_2(and_6_out), .in_3(and_7_out), .in_4(and_8_out), .in_5(1'b0), .in_6(and_1_out),
    .in_7(and_2_out), .in_8(and_3_out), .in_9(1'b0), .out_10(\n4_бітний_суматор_1_out_10 ),
    .out_11(\n4_бітний_суматор_1_out_11 ), .out_12(\n4_бітний_суматор_1_out_12 ), .out_13(_2),
    .out_14(\n4_бітний_суматор_1_out_14 ));
  and and_9 (and_9_out, a8, b4);
  and and_10 (and_10_out, a4, b4);
  and and_11 (and_11_out, a2, b4);
  and and_12 (and_12_out, a1, b4);
  and and_13 (and_13_out, a8, b8);
  and and_14 (and_14_out, a4, b8);
  and and_15 (and_15_out, a2, b8);
  and and_16 (and_16_out, a1, b8);
  \лаб_2_4_бітний_суматор  \u_4_бітний_суматор_2  (
    .in_1(and_9_out), .in_2(and_10_out), .in_3(and_11_out), .in_4(and_12_out),
    .in_5(\n4_бітний_суматор_1_out_14 ), .in_6(\n4_бітний_суматор_1_out_10 ),
    .in_7(\n4_бітний_суматор_1_out_11 ), .in_8(\n4_бітний_суматор_1_out_12 ), .in_9(1'b0),
    .out_10(\n4_бітний_суматор_2_out_10 ), .out_11(\n4_бітний_суматор_2_out_11 ),
    .out_12(\n4_бітний_суматор_2_out_12 ), .out_13(_4), .out_14(\n4_бітний_суматор_2_out_14 ));
  \лаб_2_4_бітний_суматор  \u_4_бітний_суматор_3  (
    .in_1(and_13_out), .in_2(and_14_out), .in_3(and_15_out), .in_4(and_16_out),
    .in_5(\n4_бітний_суматор_2_out_14 ), .in_6(\n4_бітний_суматор_2_out_10 ),
    .in_7(\n4_бітний_суматор_2_out_11 ), .in_8(\n4_бітний_суматор_2_out_12 ), .in_9(1'b0), .out_10(_64),
    .out_11(_32), .out_12(_16), .out_13(_8), .out_14(_128));
endmodule

module \множник_з_шифратором_та_дешифратором  (
  input  in_1,
  input  in_2,
  input  in_3,
  input  in_4,
  input  in_5,
  input  in_6,
  input  in_7,
  input  in_8,
  input  in_9,
  input  in_10,
  input  in_11,
  input  in_12,
  input  in_13,
  input  in_14,
  input  in_15,
  input  in_16,
  input  in_17,
  input  in_18,
  input  in_19,
  input  in_20,
  input  in_21
);

  wire and_1_out, controlled_buffer_1_out, controlled_buffer_2_out, controlled_buffer_3_out,
       controlled_buffer_4_out, controlled_buffer_5_out, controlled_buffer_6_out, controlled_buffer_7_out,
       controlled_buffer_8_out, not_1_out, not_2_out, not_3_out, not_4_out, not_5_out, \дешифратор_1__0 ,
       \дешифратор_1__1 , \дешифратор_1__2 , \дешифратор_1__3 , \дешифратор_1__4 , \дешифратор_1__5 ,
       \дешифратор_1__6 , \дешифратор_1__7 , \дешифратор_1__8 , \дешифратор_1__9 , \дешифратор_1__10 ,
       \дешифратор_1__11 , \дешифратор_1__12 , \дешифратор_1__13 , \дешифратор_1__14 , \дешифратор_1__15 ,
       \дешифратор_2__0 , \дешифратор_2__1 , \дешифратор_2__2 , \дешифратор_2__3 , \дешифратор_2__4 ,
       \дешифратор_2__5 , \дешифратор_2__6 , \дешифратор_2__7 , \дешифратор_2__8 , \дешифратор_2__9 ,
       \дешифратор_2__10 , \дешифратор_2__11 , \дешифратор_2__12 , \дешифратор_2__13 , \дешифратор_2__14 ,
       \дешифратор_2__15 , \множення_1_p10 , \множення_1_p11 , \множення_1_p12 , \множення_1_p13 ,
       \множення_1_p14 , \шифратор_1_q1 , \шифратор_1_q2 , \шифратор_1_q4 , \шифратор_1_q8 , \шифратор_2_q1 ,
       \шифратор_2_q2 , \шифратор_2_q4 , \шифратор_2_q8 ;

  \Шифратор  \u_шифратор_1  (
    ._0(in_1), ._1(in_2), ._2(in_3), ._3(in_4), ._4(in_5), ._5(in_5), ._6(in_7), ._7(in_8), ._8(in_9),
    ._9(in_10), .Q8(\шифратор_1_q8 ), .Q4(\шифратор_1_q4 ), .Q2(\шифратор_1_q2 ), .Q1(\шифратор_1_q1 ));
  \Шифратор  \u_шифратор_2  (
    ._0(in_11), ._1(in_12), ._2(in_13), ._3(in_14), ._4(in_15), ._5(in_16), ._6(in_18), ._7(in_19),
    ._8(in_20), ._9(in_21), .Q8(\шифратор_2_q8 ), .Q4(\шифратор_2_q4 ), .Q2(\шифратор_2_q2 ),
    .Q1(\шифратор_2_q1 ));
  LED led_1 (.in(and_1_out));
  and and_1 (and_1_out, not_1_out, not_2_out, not_4_out, not_5_out, not_5_out);
  // множення множення_1: pin names not known; wires that end beside it: \шифратор_1_q8 , \шифратор_1_q4 , \шифратор_1_q2 , \шифратор_1_q1 , \шифратор_2_q8 , \шифратор_2_q4 , \шифратор_2_q2 , \шифратор_2_q1 , in_17, \множення_1_p10 , \множення_1_p11 , \множення_1_p12 , \множення_1_p13 , \множення_1_p14 
  not not_1 (not_1_out, controlled_buffer_5_out);
  not not_2 (not_2_out, controlled_buffer_6_out);
  assign controlled_buffer_1_out = not_3_out ? \множення_1_p14  : 1'bz;  // Controlled_Buffer controlled_buffer_1
  assign controlled_buffer_2_out = not_3_out ? \множення_1_p13  : 1'bz;  // Controlled_Buffer controlled_buffer_2
  assign controlled_buffer_3_out = not_3_out ? \множення_1_p12  : 1'bz;  // Controlled_Buffer controlled_buffer_3
  assign controlled_buffer_4_out = not_3_out ? \множення_1_p11  : 1'bz;  // Controlled_Buffer controlled_buffer_4
  not not_3 (not_3_out, \множення_1_p10 );
  assign controlled_buffer_5_out = \множення_1_p10  ? \множення_1_p14  : 1'bz;  // Controlled_Buffer controlled_buffer_5
  assign controlled_buffer_6_out = \множення_1_p10  ? \множення_1_p13  : 1'bz;  // Controlled_Buffer controlled_buffer_6
  assign controlled_buffer_7_out = \множення_1_p10  ? \множення_1_p12  : 1'bz;  // Controlled_Buffer controlled_buffer_7
  not not_4 (not_4_out, controlled_buffer_7_out);
  not not_5 (not_5_out, controlled_buffer_8_out);
  assign controlled_buffer_8_out = \множення_1_p10  ? \множення_1_p11  : 1'bz;  // Controlled_Buffer controlled_buffer_8
  LED led_2 (.in(\дешифратор_1__0 ));
  \Дешифратор  \u_дешифратор_1  (
    .D1(controlled_buffer_1_out), .D2(controlled_buffer_2_out), .D3(controlled_buffer_3_out),
    .D4(controlled_buffer_4_out), ._0(\дешифратор_1__0 ), ._1(\дешифратор_1__1 ), ._2(\дешифратор_1__2 ),
    ._3(\дешифратор_1__3 ), ._4(\дешифратор_1__4 ), ._5(\дешифратор_1__5 ), ._6(\дешифратор_1__6 ),
    ._7(\дешифратор_1__7 ), ._8(\дешифратор_1__8 ), ._9(\дешифратор_1__9 ), ._10(\дешифратор_1__10 ),
    ._11(\дешифратор_1__11 ), ._12(\дешифратор_1__12 ), ._13(\дешифратор_1__13 ), ._14(\дешифратор_1__14 ),
    ._15(\дешифратор_1__15 ));
  LED led_3 (.in(\дешифратор_1__1 ));
  LED led_4 (.in(\дешифратор_1__2 ));
  LED led_5 (.in(\дешифратор_1__3 ));
  LED led_6 (.in(\дешифратор_1__4 ));
  LED led_7 (.in(\дешифратор_1__5 ));
  LED led_8 (.in(\дешифратор_1__6 ));
  LED led_9 (.in(\дешифратор_1__7 ));
  LED led_10 (.in(\дешифратор_1__8 ));
  LED led_11 (.in(\дешифратор_1__9 ));
  LED led_12 (.in(\дешифратор_1__10 ));
  LED led_13 (.in(\дешифратор_1__11 ));
  LED led_14 (.in(\дешифратор_1__12 ));
  LED led_15 (.in(\дешифратор_1__13 ));
  LED led_16 (.in(\дешифратор_1__14 ));
  LED led_17 (.in(\дешифратор_1__15 ));
  \Дешифратор  \u_дешифратор_2  (
    .D1(controlled_buffer_5_out), .D2(controlled_buffer_6_out), .D3(controlled_buffer_7_out),
    .D4(controlled_buffer_8_out), ._0(\дешифратор_2__0 ), ._1(\дешифратор_2__1 ), ._2(\дешифратор_2__2 ),
    ._3(\дешифратор_2__3 ), ._4(\дешифратор_2__4 ), ._5(\дешифратор_2__5 ), ._6(\дешифратор_2__6 ),
    ._7(\дешифратор_2__7 ), ._8(\дешифратор_2__8 ), ._9(\дешифратор_2__9 ), ._10(\дешифратор_2__10 ),
    ._11(\дешифратор_2__11 ), ._12(\дешифратор_2__12 ), ._13(\дешифратор_2__13 ), ._14(\дешифратор_2__14 ),
    ._15(\дешифратор_2__15 ));
  LED led_18 (.in(\дешифратор_2__0 ));
  LED led_19 (.in(\дешифратор_2__1 ));
  LED led_20 (.in(\дешифратор_2__2 ));
  LED led_21 (.in(\дешифратор_2__3 ));
  LED led_22 (.in(\дешифратор_2__4 ));
  LED led_23 (.in(\дешифратор_2__5 ));
  LED led_24 (.in(\дешифратор_2__6 ));
  LED led_25 (.in(\дешифратор_2__7 ));
  LED led_26 (.in(\дешифратор_2__8 ));
  LED led_27 (.in(\дешифратор_2__9 ));
  LED led_28 (.in(\дешифратор_2__10 ));
  LED led_29 (.in(\дешифратор_2__11 ));
  LED led_30 (.in(\дешифратор_2__12 ));
  LED led_31 (.in(\дешифратор_2__13 ));
  LED led_32 (.in(\дешифратор_2__14 ));
  LED led_33 (.in(\дешифратор_2__15 ));

  assign in_6 = in_5;

  // Notes on the sheet:
  //   16
  //   17
  //   18
  //   19
  //   20
  //   21
  //   22
  //   23
  //   24
  //   25
  //   26
  //   27
  //   28
  //   29
  //   30
  //   31
endmodule

module \Дешифратор  (
  input  D1,
  input  D2,
  input  D3,
  input  D4,
  output _0,
  output _1,
  output _2,
  output _3,
  output _4,
  output _5,
  output _6,
  output _7,
  output _8,
  output _9,
  output _10,
  output _11,
  output _12,
  output _13,
  output _14,
  output _15
);

  wire not_1_out, not_2_out, not_3_out, not_4_out;

  not not_1 (not_1_out, D1);
  not not_2 (not_2_out, D2);
  not not_3 (not_3_out, D3);
  not not_4 (not_4_out, D4);
  // Probe on not_1_out
  // Probe on D1
  // Probe on D2
  // Probe on not_2_out
  // Probe on D3
  // Probe on not_3_out
  // Probe on D4
  // Probe on not_4_out
  and and_1 (_0, not_1_out, not_2_out, not_3_out, not_4_out, not_4_out);
  and and_2 (_1, D1, not_2_out, not_2_out, not_3_out, not_4_out);
  and and_3 (_2, not_1_out, D2, not_3_out, not_4_out, not_4_out);
  and and_4 (_3, D1, D2, not_3_out, not_4_out, not_4_out);
  and and_5 (_4, not_1_out, not_2_out, D3, not_4_out, not_4_out);
  and and_6 (_5, D1, D1, not_2_out, D3, not_4_out);
  and and_7 (_6, not_1_out, D2, D3, not_4_out, not_4_out);
  and and_8 (_7, D1, D2, D3, not_4_out, not_4_out);
  and and_9 (_8, D4, not_3_out, not_2_out, not_1_out, not_1_out);
  and and_10 (_9, D1, not_2_out, not_3_out, D4, D4);
  and and_11 (_10, not_1_out, D2, not_3_out, D4, D4);
  and and_12 (_11, D1, D2, not_3_out, D4, D4);
  and and_13 (_12, not_1_out, not_2_out, D3, D4, D4);
  and and_14 (_13, D1, not_2_out, D3, D4, D4);
  and and_15 (_14, not_1_out, D2, D3, D4, D4);
  and and_16 (_15, D1, D2, D3, D4, D4);

  // Notes on the sheet:
  //   D1~D1
  //   D2~D2
  //   D4~D4
  //   D8~D8
endmodule

module _5 (
  input  in_1,
  input  in_2,
  input  in_3,
  input  in_4,
  input  in_5,
  input  in_6,
  input  in_7,
  input  in_8,
  input  in_9,
  input  in_10,
  input  in_11,
  input  in_12,
  input  in_13,
  input  in_14,
  input  in_15,
  input  in_16,
  input  in_17,
  input  in_18,
  input  in_19,
  input  in_20,
  input  in_21
);

  wire and_1_out, and_2_out, and_3_out, and_4_out, and_5_out, and_6_out, and_7_out, and_8_out, CL_out,
       nor_1_out, not_1_out, not_2_out, R_out, shift_register_1_q0, shift_register_1_q1, shift_register_1_q2,
       shift_register_1_q3, shift_register_2_q0, shift_register_2_q1, shift_register_2_q2,
       shift_register_2_q3, shift_register_2_q4, shift_register_2_q5, shift_register_2_q6,
       shift_register_2_q7, \шифратор_1_q1 , \шифратор_1_q2 , \шифратор_1_q4 , \шифратор_1_q8 ,
       \шифратор_2_q1 , \шифратор_2_q2 , \шифратор_2_q4 , \шифратор_2_q8 ;
  wire [7:0] \n8_бітний_суматор_1_out_26 , register_1_q;

  \Шифратор  \u_шифратор_1  (
    ._0(in_1), ._1(in_2), ._2(in_3), ._3(in_4), ._4(in_5), ._5(in_5), ._6(in_7), ._7(in_8), ._8(in_9),
    ._9(in_10), .Q8(\шифратор_1_q8 ), .Q4(\шифратор_1_q4 ), .Q2(\шифратор_1_q2 ), .Q1(\шифратор_1_q1 ));
  \Шифратор  \u_шифратор_2  (
    ._0(in_11), ._1(in_12), ._2(in_13), ._3(in_14), ._4(in_15), ._5(in_16), ._6(in_17), ._7(in_18),
    ._8(in_19), ._9(in_20), .Q8(\шифратор_2_q8 ), .Q4(\шифратор_2_q4 ), .Q2(\шифратор_2_q2 ),
    .Q1(\шифратор_2_q1 ));
  LED led_1 (.in(nor_1_out));
  nor nor_1 (nor_1_out, shift_register_1_q0, shift_register_1_q1, shift_register_1_q2, shift_register_1_q3);
  not not_1 (not_1_out, in_21);
  Button CL (.out(CL_out));
  Button R (.out(R_out));
  Shift_Register #(.length(4)) shift_register_1 (
    .shift(not_1_out), .in(1'b0), .clk(CL_out), .load(in_21), .clr(R_out), .d0(\шифратор_1_q8 ),
    .q0(shift_register_1_q0), .d1(\шифратор_1_q4 ), .q1(shift_register_1_q1), .d2(\шифратор_1_q2 ),
    .q2(shift_register_1_q2), .d3(\шифратор_1_q1 ), .q3(shift_register_1_q3));  // open: out
  Shift_Register shift_register_2 (
    .shift(not_1_out), .in(1'b0), .clk(CL_out), .load(in_21), .clr(R_out), .d0(\шифратор_2_q1 ),
    .q0(shift_register_2_q0), .d1(\шифратор_2_q2 ), .q1(shift_register_2_q1), .d2(\шифратор_2_q4 ),
    .q2(shift_register_2_q2), .d3(\шифратор_2_q8 ), .q3(shift_register_2_q3), .d4(1'b0),
    .q4(shift_register_2_q4), .d5(1'b0), .q5(shift_register_2_q5), .d6(1'b0), .q6(shift_register_2_q6),
    .d7(1'b0), .q7(shift_register_2_q7));  // open: out
  and and_1 (and_1_out, shift_register_1_q3, shift_register_2_q7);
  and and_2 (and_2_out, shift_register_1_q3, shift_register_2_q6);
  and and_3 (and_3_out, shift_register_1_q3, shift_register_2_q5);
  and and_4 (and_4_out, shift_register_1_q3, shift_register_2_q4);
  and and_5 (and_5_out, shift_register_1_q3, shift_register_2_q3);
  and and_6 (and_6_out, shift_register_1_q3, shift_register_2_q2);
  and and_7 (and_7_out, shift_register_1_q3, shift_register_2_q1);
  and and_8 (and_8_out, shift_register_1_q3, shift_register_2_q0);
  \_8_бітний_суматор  \u_8_бітний_суматор_1  (
    ._124(and_1_out), ._64(and_2_out), ._32(and_3_out), ._16(and_4_out), ._8(and_5_out), ._4(and_6_out),
    ._2(and_7_out), ._1(and_8_out), ._124_2(register_1_q[7]), ._64_2(register_1_q[6]),
    ._32_2(register_1_q[5]), ._16_2(register_1_q[4]), ._8_2(register_1_q[3]), ._4_2(register_1_q[2]),
    ._2_2(register_1_q[1]), ._1_2(register_1_q[0]), .p(1'b0), .out_19(\n8_бітний_суматор_1_out_26 [7]),
    .out_20(\n8_бітний_суматор_1_out_26 [6]), .out_21(\n8_бітний_суматор_1_out_26 [5]),
    .out_22(\n8_бітний_суматор_1_out_26 [4]), .out_23(\n8_бітний_суматор_1_out_26 [3]),
    .out_24(\n8_бітний_суматор_1_out_26 [2]), .out_25(\n8_бітний_суматор_1_out_26 [1]),
    .out_26(\n8_бітний_суматор_1_out_26 [0]));  // open: out_18
  not not_2 (not_2_out, in_21);
  Register register_1 (.D(\n8_бітний_суматор_1_out_26 ), .en(not_2_out), .Q(register_1_q), .clk(CL_out), .clr(R_out));
  // Probe on register_1_q

  assign in_6 = in_5;

  // Notes on the sheet:
  //   Final
endmodule

module \_8_бітний_суматор  (
  input  _124,
  input  _64,
  input  _32,
  input  _16,
  input  _8,
  input  _4,
  input  _2,
  input  _1,
  input  _124_2,
  input  _64_2,
  input  _32_2,
  input  _16_2,
  input  _8_2,
  input  _4_2,
  input  _2_2,
  input  _1_2,
  input  p,
  output out_18,
  output out_19,
  output out_20,
  output out_21,
  output out_22,
  output out_23,
  output out_24,
  output out_25,
  output out_26
);

  wire \n4_бітний_суматор_2_out_14 ;

  \лаб_2_4_бітний_суматор  \u_4_бітний_суматор_1  (
    .in_1(_124), .in_2(_64), .in_3(_32), .in_4(_16), .in_5(_124_2), .in_6(_64_2), .in_7(_32_2), .in_8(_16_2),
    .in_9(\n4_бітний_суматор_2_out_14 ), .out_10(out_18), .out_11(out_19), .out_12(out_20), .out_13(out_21),
    .out_14(out_26));
  \лаб_2_4_бітний_суматор  \u_4_бітний_суматор_2  (
    .in_1(_8), .in_2(_4), .in_3(_2), .in_4(_1), .in_5(_8_2), .in_6(_4_2), .in_7(_2_2), .in_8(_1_2), .in_9(p),
    .out_10(out_22), .out_11(out_23), .out_12(out_24), .out_13(out_25), .out_14(\n4_бітний_суматор_2_out_14 ));
endmodule

module \ділення  (
  input  Z0,
  input  Z1,
  input  Z2,
  input  Z3,
  input  d0,
  input  d1,
  input  d2,
  input  d3,
  input  in_9,
  input  Z4,
  input  Z5,
  input  Z6,
  output out_13,
  output out_14,
  output out_15,
  output out_16,
  output out_17,
  output out_18,
  output out_19,
  output out_20
);

  wire xor_1_out, xor_2_out, xor_3_out, xor_4_out, xor_5_out, xor_6_out, xor_7_out, xor_8_out, xor_9_out,
       xor_10_out, xor_11_out, xor_12_out, xor_13_out, xor_14_out, xor_15_out, xor_16_out,
       \повний_суматор_5_p , \повний_суматор_5_s , \повний_суматор_6_p , \повний_суматор_7_p ,
       \повний_суматор_7_s , \повний_суматор_8_p , \повний_суматор_8_s , \повний_суматор_9_p ,
       \повний_суматор_9_s , \повний_суматор_10_p , \повний_суматор_10_s , \повний_суматор_11_p ,
       \повний_суматор_11_s , \повний_суматор_12_p , \повний_суматор_13_p , \повний_суматор_13_s ,
       \повний_суматор_14_p , \повний_суматор_14_s , \повний_суматор_15_p , \повний_суматор_15_s ,
       \повний_суматор_16_p ;

  Hex_Digit_Display hex_digit_display_1 (.value({out_16, out_15, out_14, out_13}));  // open: dp
  ExactlyOne xor_1 (.out(xor_1_out), .in2(in_9), .in3(d0), .in4(d0));
  ExactlyOne xor_2 (.out(xor_2_out), .in1(out_13), .in3(d0), .in4(d0));
  xor xor_3 (xor_3_out, out_14, d0);
  xor xor_4 (xor_4_out, out_15, d0);
  \Повний_суматор  \u_повний_суматор_1  (.Pi(\повний_суматор_7_p ), .a(xor_1_out), .b(Z0), .P(out_13));  // open: S
  \Повний_суматор  \u_повний_суматор_2  (
    .Pi(\повний_суматор_8_p ), .a(xor_2_out), .b(\повний_суматор_7_s ), .P(out_14));  // open: S
  \Повний_суматор  \u_повний_суматор_3  (
    .Pi(\повний_суматор_5_p ), .a(xor_3_out), .b(\повний_суматор_8_s ), .P(out_15));  // open: S
  \Повний_суматор  \u_повний_суматор_4  (
    .Pi(\повний_суматор_6_p ), .a(xor_4_out), .b(\повний_суматор_5_s ), .S(out_17), .P(out_16));
  xor xor_5 (xor_5_out, in_9, d1);
  xor xor_6 (xor_6_out, out_13, d1);
  xor xor_7 (xor_7_out, out_14, d1);
  xor xor_8 (xor_8_out, out_15, d1);
  \Повний_суматор  \u_повний_суматор_5  (
    .Pi(\повний_суматор_11_p ), .a(xor_7_out), .b(\повний_суматор_10_s ), .S(\повний_суматор_5_s ),
    .P(\повний_суматор_5_p ));
  \Повний_суматор  \u_повний_суматор_6  (
    .Pi(\повний_суматор_12_p ), .a(xor_8_out), .b(\повний_суматор_11_s ), .S(out_18), .P(\повний_суматор_6_p ));
  xor xor_9 (xor_9_out, in_9, d2);
  \Повний_суматор  \u_повний_суматор_7  (
    .Pi(\повний_суматор_9_p ), .a(xor_5_out), .b(Z1), .S(\повний_суматор_7_s ), .P(\повний_суматор_7_p ));
  xor xor_10 (xor_10_out, out_13, d2);
  \Повний_суматор  \u_повний_суматор_8  (
    .Pi(\повний_суматор_10_p ), .a(xor_6_out), .b(\повний_суматор_9_s ), .S(\повний_суматор_8_s ),
    .P(\повний_суматор_8_p ));
  xor xor_11 (xor_11_out, out_14, d2);
  xor xor_12 (xor_12_out, out_15, d2);
  xor xor_13 (xor_13_out, out_13, d3);
  xor xor_14 (xor_14_out, out_14, d3);
  xor xor_15 (xor_15_out, out_15, d3);
  xor xor_16 (xor_16_out, in_9, d3);
  \Повний_суматор  \u_повний_суматор_9  (
    .Pi(\повний_суматор_13_p ), .a(xor_9_out), .b(Z2), .S(\повний_суматор_9_s ), .P(\повний_суматор_9_p ));
  \Повний_суматор  \u_повний_суматор_10  (
    .Pi(\повний_суматор_14_p ), .a(xor_10_out), .b(\повний_суматор_13_s ), .S(\повний_суматор_10_s ),
    .P(\повний_суматор_10_p ));
  \Повний_суматор  \u_повний_суматор_11  (
    .Pi(\повний_суматор_15_p ), .a(xor_11_out), .b(\повний_суматор_14_s ), .S(\повний_суматор_11_s ),
    .P(\повний_суматор_11_p ));
  \Повний_суматор  \u_повний_суматор_12  (
    .Pi(\повний_суматор_16_p ), .a(xor_12_out), .b(\повний_суматор_15_s ), .S(out_19),
    .P(\повний_суматор_12_p ));
  \Повний_суматор  \u_повний_суматор_13  (
    .Pi(Z3), .a(xor_16_out), .b(in_9), .S(\повний_суматор_13_s ), .P(\повний_суматор_13_p ));
  \Повний_суматор  \u_повний_суматор_14  (
    .Pi(Z4), .a(xor_13_out), .b(out_13), .S(\повний_суматор_14_s ), .P(\повний_суматор_14_p ));
  \Повний_суматор  \u_повний_суматор_15  (
    .Pi(Z5), .a(xor_14_out), .b(out_14), .S(\повний_суматор_15_s ), .P(\повний_суматор_15_p ));
  \Повний_суматор  \u_повний_суматор_16  (.Pi(Z6), .a(xor_15_out), .b(out_15), .S(out_20), .P(\повний_суматор_16_p ));
endmodule
